// Logisim project cpu.circ as structural Verilog: 2 circuits, main circuit main
module main (
  input  [15:0] From_Instr_Mem,
  input  clk,
  output [15:0] r0,
  output [15:0] r1,
  output [15:0] r2,
  output [15:0] r3,
  output [15:0] Display_0,
  output [15:0] Display_1,
  output [15:0] To_Instr_Mem,
  output [15:0] Data_Mem_Data,
  output [15:0] Data_Mem_Addr,
  output Data_Mem_Write
);


  // Other names for the same wires on the sheet: d0[15:0] = Display_0; d1[15:0] = Display_1

  // Notes on the sheet:
  //   This is the current PC that you need to send as OUTPUT
  //   This is the instruction that you would receive as INPUT
  //   This is a CLK that is an INPUT driven from the harness.
  //   Remember, this circuit is loaded from the harness to be tested!
  //   DO NOT CHANGE THE LOCATIONS OF THE INPUTS OR OUTPUTS! IF YOU DO SO, YOU NEED TO MAKE SURE THE PINS ARE IN THE RIGHT PLACES!
  //   These are OUTPUTS of the circuit
  //   These are OUTPUTS of the circuit
endmodule

module control (
  input  [15:0] opcode_funct,
  input  Equal,
  output [1:0] nPC_sel,
  output RegDst,
  output ExtOp,
  output RegWr,
  output ALUSrc,
  output [3:0] ALUctr,
  output MemtoReg,
  output MemWr
);

  wire not_1_out;
  wire [1:0] eq, neq;
  wire [3:0] aluop;

  assign eq = {{1{1'b0}}, Equal};  // Bit_Extender bit_extender_1
  not not_1 (not_1_out, Equal);
  assign neq = {{1{1'b0}}, not_1_out};  // Bit_Extender bit_extender_2
  Multiplexer #(.select(4), .enable("false")) multiplexer_1 (
    .in0(1'b0), .in1(1'b0), .in2(1'b0), .in3(1'b0), .in4(1'b0), .in5(1'b0), .in6(1'b0), .in7(1'b0),
    .in8(1'b0), .in9(1'b1), .in10(1'b0), .in11(1'b1), .in12(1'b0), .out(MemtoReg), .sel(opcode_funct[15:12]));  // open: in13, in14, in15
  Multiplexer #(.select(4), .enable("false")) multiplexer_2 (
    .in0(1'b0), .in1(1'b0), .in2(1'b0), .in3(1'b0), .in4(1'b0), .in5(1'b0), .in6(1'b0), .in7(1'b0),
    .in8(1'b0), .in9(1'b1), .in10(1'b0), .in11(1'b0), .in12(1'b0), .out(MemWr), .sel(opcode_funct[15:12]));  // open: in13, in14, in15
  Comparator #(.width(4)) comparator_1 (.a(opcode_funct[15:12]), .b(4'b0000), .eq(RegDst));  // open: gt, lt
  Multiplexer #(.select(4), .enable("false")) multiplexer_3 (
    .in0(1'b0), .in1(1'b0), .in2(1'b0), .in3(1'b0), .in4(1'b1), .in5(1'b1), .in6(1'b0), .in7(1'b0),
    .in8(1'b1), .in9(1'b1), .in10(1'b0), .in11(1'b1), .in12(1'b0), .out(ExtOp), .sel(opcode_funct[15:12]));  // open: in13, in14, in15
  Multiplexer #(.select(4), .enable("false")) multiplexer_4 (
    .in0(1'b0), .in1(1'b0), .in2(1'b0), .in3(1'b0), .in4(1'b1), .in5(1'b1), .in6(1'b1), .in7(1'b1),
    .in8(1'b1), .in9(1'b1), .in10(1'b1), .in11(1'b1), .in12(1'b1), .out(ALUSrc), .sel(opcode_funct[15:12]));  // open: in13, in14, in15
  Multiplexer #(.width(4), .enable("false")) multiplexer_5 (
    .in0(aluop), .in1(opcode_funct[3:0]), .sel(RegDst));  // open: out
  Multiplexer #(.select(4), .enable("false")) multiplexer_6 (
    .in0(1'b1), .in1(1'b1), .in2(1'b0), .in3(1'b0), .in4(1'b0), .in5(1'b1), .in6(1'b1), .in7(1'b1),
    .in8(1'b0), .in9(1'b0), .in10(1'b1), .in11(1'b1), .in12(1'b0), .out(RegWr), .sel(opcode_funct[15:12]));  // open: in13, in14, in15
  Multiplexer #(.select(4), .width(4), .enable("false")) multiplexer_7 (
    .in0(opcode_funct[3:0]), .in1(4'b1111), .in2(4'b1111), .in3(4'b1111), .in4(4'b1111), .in5(4'b0000),
    .in6(4'b0111), .in7(4'b0110), .in8(4'b1111), .in9(4'b0000), .in10(4'b0010), .in11(4'b0000),
    .in12(4'b1111), .out(ALUctr), .sel(opcode_funct[15:12]));  // open: in13, in14, in15
  Multiplexer #(.select(4), .width(2), .enable("false")) multiplexer_8 (
    .in0(2'b00), .in1(2'b10), .in2(2'b10), .in3(2'b10), .in4(eq), .in5(2'b00), .in6(2'b00), .in7(2'b00),
    .in8(neq), .in9(2'b00), .in10(2'b00), .in11(2'b00), .in12(2'b00), .out(nPC_sel), .sel(opcode_funct[15:12]));  // open: in13, in14, in15

  // Other names for the same wires on the sheet: ac[3:0] = ALUctr; as = ALUSrc; eo = ExtOp; isR = RegDst;
  //   mtr = MemtoReg; mw = MemWr; nps[1:0] = nPC_sel; func[5:0] = opcode_funct[5:0]; op[3:0] = opcode_funct[15:12];
  //   rw = RegWr

  // Notes on the sheet:
  //   Determine MemtoReg
  //   Determine MemWr
  //   Determine ExtOp
  //   Determine ALUSrc
  //   Determine RegWr
  //   Determine ALUctr
  //   Determine ALUctr
  //   00 if PC+4, 01 if branch, 10 if jump
  //   Low if rt, high if rd
  //   Low if zero, high if sign
  //   High if register, low if immediate
  //   High if memory, low if alu
endmodule
